# Fritzing sketch module_io (saved by Fritzing 0.9.3b)
circuit board: 4.86336cm x 6.03586cm
stripboards: 1

parts:
  U1 = 74HC595 [package="DIP16 [THT]"]
  J1 = female pin header, 2 pins [form="♀ (female)"]
  J2 = female pin header, 2 pins [form="♀ (female)"]
  J3 = female pin header, 2 pins [form="♀ (female)"]
  J4 = female pin header, 2 pins [form="♀ (female)"]
  U2 = 74HC595 [package="DIP16 [THT]"]
  J5 = female pin header, 2 pins [form="♀ (female)"]
  J6 = female pin header, 2 pins [form="♀ (female)"]
  J7 = female pin header, 2 pins [form="♀ (female)"]
  J8 = female pin header, 2 pins [form="♀ (female)"]
  J9 = female pin header, 2 pins [form="♀ (female)"]
  R1 = Resistor [tolerance=±5% resistance=1k package=THT]
  R2 = Resistor [tolerance=±5% resistance=1k package=THT]
  R3 = Resistor [tolerance=±5% resistance=1k package=THT]
  R4 = Resistor [tolerance=±5% resistance=1k package=THT]
  J10 = female pin header, 2 pins [form="♀ (female)"]
  J11 = female pin header, 2 pins [form="♀ (female)"]

nets:
  N1: U1.Q1, J4.pin1
  N2: U1.Q2, J4.pin2
  N3: U1.Q3, J3.pin1
  N4: U1.Q4, J3.pin2
  N5: U1.Q5, J2.pin1
  N6: U1.Q6, J2.pin2
  N7: U1.Q7, J1.pin1
  N8: U1.GND, J1.pin2
  VCC: U1.MR, U1.VCC, U2.VCC, J5.pin2, R1.Pin_0, R2.Pin_0, R3.Pin_0, R4.Pin_0
  N9: U1.SH_CP, U2.Q2, J6.pin2
  N10: U1.ST_CP, J6.pin1
  N11: U1.DS, J10.pin1
  N12: U2.Q1, J5.pin1
  N13: U2.Q3, J8.pin1, R1.Pin_1
  N14: U2.Q4, J8.pin2, R2.Pin_1
  N15: U2.Q5, J9.pin1, R3.Pin_1
  N16: U2.Q6, J9.pin2, R4.Pin_1
  N17: U2.GND, J7.pin2
  N18: U2.Q7', J10.pin2
  N19: U2.MR, J11.pin2
