# Fritzing sketch module_io_take2 (saved by Fritzing 0.9.3b)
circuit board: 3.08756cm x 5.00967cm
stripboards: 1

parts:
  U2 = 74HC595 [package="DIP16 [THT]"]
  J1 = female pin header, 2 pins [form="♀ (female)"]
  J2 = female pin header, 2 pins [form="♀ (female)"]
  J3 = female pin header, 2 pins [form="♀ (female)"]
  J4 = female pin header, 2 pins [form="♀ (female)"]
  J5 = female pin header, 2 pins [form="♀ (female)"]
  J6 = female pin header, 2 pins [form="♀ (female)"]
  J7 = female pin header, 2 pins [form="♀ (female)"]
  J8 = female pin header, 2 pins [form="♀ (female)"]
  J9 = female pin header, 2 pins [form="♀ (female)"]
  U3 = mystery part, 2 pins [chip_label=?]
  U4 = mystery part, 2 pins [chip_label=?]
  U5 = mystery part, 2 pins [chip_label=?]
  U6 = mystery part, 2 pins [chip_label=?]
  U7 = 74HC595 [package="DIP16 [THT]"]

nets:
  N1: U2.Q1, J6.pin1
  N2: U2.Q2, J6.pin2
  N3: U2.Q3, J7.pin1
  N4: U2.Q4, J7.pin2
  N5: U2.Q5, J8.pin1
  N6: U2.Q6, J8.pin2
  N7: U2.Q7, J9.pin1
  GND: U2.GND, U2.OE, J3.pin2, J9.pin2, U7.GND
  N8: U2.Q7', J3.pin1
  VCC: U2.MR, U2.VCC, J1.pin2, U3.pin1, U4.pin1, U5.pin1, U6.pin1, U7.VCC
  N9: U2.SH_CP, J2.pin2, U7.Q2
  N10: U2.ST_CP, J2.pin1
  N11: J1.pin1, U7.Q1
  N12: J4.pin1, U3.pin2, U7.Q3
  N13: J4.pin2, U4.pin2, U7.Q4
  N14: J5.pin1, U5.pin2, U7.Q5
  N15: J5.pin2, U6.pin2, U7.Q6

notes:
  HC165
