# Fritzing sketch module_io_take3 (saved by Fritzing 0.9.3b)
circuit board: 2.8cm x 5.4cm
stripboards: 1

parts:
  U2 = 74HC595 [package="DIP16 [THT]"]
  J4 = female pin header, 2 pins [form="♀ (female)"]
  J5 = female pin header, 2 pins [form="♀ (female)"]
  J6 = female pin header, 2 pins [form="♀ (female)"]
  J7 = female pin header, 2 pins [form="♀ (female)"]
  J8 = female pin header, 2 pins [form="♀ (female)"]
  J9 = female pin header, 2 pins [form="♀ (female)"]
  U4 = mystery part, 2 pins [chip_label=?]
  U5 = mystery part, 2 pins [chip_label=?]
  U6 = mystery part, 2 pins [chip_label=?]
  U7 = 74HC595 [package="DIP16 [THT]"]
  J10 = female pin header, 2 pins [form="♀ (female)"]
  U9 = mystery part, 2 pins [chip_label=?]
  J11 = female pin header, 2 pins [form="♀ (female)"]
  U10 = mystery part, 2 pins [chip_label=?]
  U12 = mystery part, 2 pins [chip_label=?]
  U13 = mystery part, 2 pins [chip_label=?]
  J12 = female pin header, 2 pins [form="♀ (female)"]
  J13 = female pin header, 2 pins [form="♀ (female)"]
  J14 = female pin header, 2 pins [form="♀ (female)"]
  U3 = mystery part, 2 pins [chip_label=?]

nets:
  N1: U2.Q1, J6.pin1
  N2: U2.Q2, J6.pin2
  N3: U2.Q3, J7.pin1
  N4: U2.Q4, J7.pin2
  N5: U2.Q5, J8.pin1
  N6: U2.Q6, J8.pin2
  N7: U2.Q7, J9.pin1
  GND: U2.GND, U2.OE, J9.pin2, U7.GND, J12.pin1
  VCC: U2.MR, U2.VCC, U4.pin1, U5.pin1, U6.pin1, U7.VCC, U9.pin2, U10.pin2, U12.pin2, U13.pin2, J14.pin1, U3.pin1
  N8: U2.SH_CP, U7.Q2, J13.pin1
  N9: U2.ST_CP, J12.pin2
  N10: J4.pin1, U7.Q3, U3.pin2
  N11: J4.pin2, U4.pin2, U7.Q4
  N12: J5.pin1, U5.pin2, U7.Q5
  N13: J5.pin2, U6.pin2, U7.Q6
  N14: U7.Q1, J13.pin2
  N15: U7.SH_CP, J10.pin1, U12.pin1
  N16: U7.ST_CP, J10.pin2, U9.pin1
  N17: U7.OE, J11.pin1, U13.pin1
  N18: U7.DS, J11.pin2, U10.pin1
  N19: U7.Q0, J14.pin2

notes:
  HC165
